// Logisim project ELEVADOR.circ as structural Verilog: 1 circuit, main circuit main
module main (
  input  S9,
  input  S8,
  input  S7,
  input  S6,
  input  S5,
  input  S4,
  input  S3,
  input  S2,
  input  S1,
  input  S0
);

  wire K0, K1, K2, K3, L7, L8;
  wire [3:0] HEX0, HEX2, HEX3, HEX4, HEX5;

  Hex_Digit_Display hex_digit_display_1 (.value(HEX5));  // open: dp
  Hex_Digit_Display hex_digit_display_2 (.value(HEX4));  // open: dp
  LED L9 (.in(S9));
  LED u_L8 (.in(L8));
  LED u_L7 (.in(L7));
  Hex_Digit_Display hex_digit_display_3 (.value(HEX3));  // open: dp
  LED L6 (.in(1'b0));
  LED L4 (.in(S4));
  LED L5 (.in(S5));
  // VHDL_Entity #(.content("library ieee;\nuse ieee.std_logic_1164.all;\nuse ieee.numeric_std.all;\n\nentity elevador is\n    port (\n        andar_requisitado: in std_logic_vector(3 downto 0);\n        --requisitado indica se tem alguem chamando o elevador\n        clk, requisitado, rst: in std_logic;\n        --posicao atual do elevador\n        posicao_output: out std_logic_vector(3 downto 0) := \"0000\";\n        --direcao: '0' indica descendo, '1' indica subindo\n        direcao: out std_logic := '0';\n        --andando: '0' indica parado, '1' indica que esta andando\n        andando: out std_logic := '0'\n    );\n\nend elevador;\n\narchitecture arch_elevador of elevador is\n\n    type state_t is (up, down, stop);\n\n    --signal andar : integer range 0 to 15 := 0;\n    signal current_state : state_t := stop;\n    signal next_state : state_t := stop;\n    signal destino : std_logic_vector(3 downto 0) := \"0000\";\n\n    signal posicao : std_logic_vector(3 downto 0) := \"0000\";\n\n    constant subindo : std_logic := '1';\n    constant descendo : std_logic := '0';\n\nbegin\n\n    impr:process(current_state, next_state, destino, posicao) is\n    begin\n		if (current_state'EVENT) then\n	    	report \"----------> CHANGE IN current_state: \" & state_t'image(current_state);\n		elsif (next_state'EVENT) then\n			report \"----------> CHANGE IN next_state: \" & state_t'image(next_state);\n	  	--elsif (destino'EVENT) then\n			--report \"----------> CHANGE IN DESTINO: \" & unsigned'image(unsigned(destino));\n		--elsif (posicao'EVENT) then\n			--report \"----------> CHANGE IN POSICAO: \" & unsigned'image(unsigned(posicao));\n		end if;\n    end process impr;\n\n    comb:process(clk) is \n    begin\n        if rising_edge(clk) then\n\n            next_state <= current_state;\n            posicao_output <= posicao;\n\n            case current_state is \n                when stop =>\n\n                    andando <= '0';\n\n				-- if requisitado = '1' and posicao /= destino then\n                    if posicao /= destino then\n\n                        if posicao < destino then\n                            next_state <= up;\n                        else \n                            next_state <= down;\n                        end if;\n\n                    end if;\n\n                when up =>\n\n                    if posicao = destino then\n                        next_state <= stop;\n                    end if;\n\n                    andando <= '1';\n                    direcao <= subindo;\n\n                when down =>\n\n                    if posicao = destino then \n                        next_state <= stop;\n                    end if;\n\n                    andando <= '1';\n                    direcao <= descendo;\n\n            end case;\n        end if;\n\n    end process comb;\n\n    mem:process(clk) is \n    begin\n        if rst = '1' then\n\n            current_state <= stop;\n            -- andando <= '0';\n            posicao <= \"0000\";\n            destino <= \"0000\";\n\n        elsif falling_edge(clk) then\n			if requisitado = '1' then\n				destino <= andar_requisitado;\n			end if;\n			\n            current_state <= next_state;\n\n            if next_state = up then\n                posicao <= std_logic_vector(unsigned(posicao) + 1);\n            elsif next_state = down then\n                posicao <= std_logic_vector(unsigned(posicao) - 1);\n            end if;\n\n        end if;\n\n    end process mem;\n\n    \n\nend arch_elevador;")) vhdl_entity_1: pin names not known; wires that end beside it: {S4, S3, S2, S1}, S9, S5, S0, HEX0, L7, L8
  Hex_Digit_Display hex_digit_display_4 (.value(HEX2));  // open: dp
  Hex_Digit_Display hex_digit_display_5 (.value({S4, S3, S2, S1}));  // open: dp
  LED L2 (.in(S2));
  LED L3 (.in(S3));
  Hex_Digit_Display hex_digit_display_6 (.value(HEX0));  // open: dp
  LED L1 (.in(S1));
  LED L0 (.in(S0));
  Button u_K3 (.out(K3));
  Button u_K2 (.out(K2));
  Button u_K1 (.out(K1));
  Button u_K0 (.out(K0));

  // Other names for the same wires on the sheet: HEX1[3:0] = {S4, S3, S2, S1}; L1 = S1; L2 = S2; L3 = S3; L4 = S4;
  //   L0 = S0; L5 = S5; L9 = S9
endmodule
