// Logisim project MAQ REFRI.circ as structural Verilog: 1 circuit, main circuit main
module main (
  input  S9,
  input  S8,
  input  S7,
  input  S6,
  input  S5,
  input  S4,
  input  S3,
  input  S2,
  input  S1,
  input  S0
);

  wire K0, K1, K2, K3, L7, L8;
  wire [3:0] HEX1, HEX2, HEX3, HEX4, HEX5;

  Hex_Digit_Display hex_digit_display_1 (.value(HEX5));  // open: dp
  Hex_Digit_Display hex_digit_display_2 (.value(HEX4));  // open: dp
  LED L9 (.in(S9));
  LED u_L8 (.in(L8));
  LED u_L7 (.in(L7));
  Hex_Digit_Display hex_digit_display_3 (.value(HEX3));  // open: dp
  LED L6 (.in(1'b0));
  LED L4 (.in(S4));
  LED L5 (.in(S5));
  // VHDL_Entity #(.content("library ieee;\nuse ieee.std_logic_1164.all;\nuse ieee.numeric_std.all;\n\nentity maq_refri is\n    -- entrada: 0: nada, 2: 10 cent, 3: 25 cent, 4 : 50 cent, 5: 1 real\n    port (\n        entrada : in std_logic_vector(2 downto 0) := \"000\";\n        botao, rst, clk : in std_logic;\n        refri : out std_logic := '0';\n        devolve : out std_logic := '0'\n    );\n\nend maq_refri;\n\narchitecture arch_refri of maq_refri is\n\n    --Estados possiveis da maquina\n    type state_t is (refri_idle, refri_give, refri_reset);\n\n    signal current_state : state_t := refri_idle;\n    signal next_state : state_t := refri_idle;\n    signal grana_total : integer range 0 to 63 := 0;\n\nbegin\n\n    --Processo que imprime informacoes relevantes da maquina no console\n    impr:process(current_state, next_state, grana_total, botao) is\n	begin\n		if (current_state'EVENT) then\n	    		report \"----------> CHANGE IN current_state: \" & state_t'image(current_state);\n	  	elsif (next_state'EVENT) then\n	  		report \"----------> CHANGE IN next_state: \" & state_t'image(next_state);\n	  	elsif (grana_total'EVENT) then\n	  		report \"----------> CHANGE IN GRANA: \" & integer'image(grana_total);\n	  	elsif (botao'EVENT) then\n	  		report \"----------> CHANGE IN BOTAO: \" & std_logic'image(botao);\n	  	end if;\n	end process;\n\n    --Processo que cuida da logica combinacional da maquina de refrigerante\n    comb:process(clk) is\n    begin\n        if falling_edge(clk) then\n            next_state <= current_state;\n            \n            case current_state is\n                when refri_idle =>\n\n                    devolve <= '0';\n                    refri <= '0';\n\n                    if botao = '1' then\n\n                        if grana_total = 20 then\n                            next_state <= refri_give;\n                        else\n                            next_state <= refri_reset;\n                        end if;\n\n                    else \n                        if grana_total > 20 then\n                            next_state <= refri_reset;\n                        else \n                            next_state <= refri_idle;\n                        end if;\n\n                    end if;\n\n                    \n                when refri_give =>\n\n                    devolve <= '0';\n                    refri <= '1';\n\n                    next_state <= refri_idle;\n                    \n                when refri_reset =>\n                    devolve <= '1';\n                    next_state <= refri_idle;\n            end case;\n\n        end if;\n    end process comb;\n\n    --Processo que cuida da logica da memoria da maquina de refrigerante\n    mem:process(rst, clk) is\n    begin\n        if rising_edge(clk) then\n\n            if rst = '1' then\n                current_state <= refri_idle;\n            else\n                current_state <= next_state;\n\n            end if;\n\n            if next_state = refri_reset or next_state = refri_give or rst = '1' then\n                grana_total <= 0;\n            else \n                case entrada is\n\n                    when \"010\" =>\n                        grana_total <= grana_total + 2;\n                    when \"011\" =>\n                        grana_total <= grana_total + 5;\n                    when \"100\" => \n                        grana_total <= grana_total + 10;\n                    when \"101\" => \n                        grana_total <= grana_total + 20;\n                    when others =>\n                        null;\n                end case;\n\n            end if;\n        end if;\n    end process mem;\nend arch_refri;")) vhdl_entity_1: pin names not known; wires that end beside it: {S3, S2, S1}, S4, S0, S9, L7, L8
  Hex_Digit_Display hex_digit_display_4 (.value(HEX2));  // open: dp
  Hex_Digit_Display hex_digit_display_5 (.value(HEX1));  // open: dp
  LED L2 (.in(S2));
  LED L3 (.in(S3));
  Hex_Digit_Display hex_digit_display_6 (.value({1'b0, S3, S2, S1}));  // open: dp
  LED L1 (.in(S1));
  LED L0 (.in(S0));
  Button u_K3 (.out(K3));
  Button u_K2 (.out(K2));
  Button u_K1 (.out(K1));
  Button u_K0 (.out(K0));

  // Other names for the same wires on the sheet: HEX0[2:0] = {S3, S2, S1}; L1 = S1; L2 = S2; L3 = S3; L0 = S0;
  //   L4 = S4; L5 = S5; L9 = S9
endmodule
