// Logisim project DE0_CV_Evolution.circ as structural Verilog: 1 circuit, main circuit main
module main (
  input  S9,
  input  S8,
  input  S7,
  input  S6,
  input  S5,
  input  S4,
  input  S3,
  input  S2,
  input  S1,
  input  S0
);

  wire K0, K1, K2, K3;
  wire [3:0] HEX0, HEX1, HEX2, HEX3, HEX4, HEX5;

  Hex_Digit_Display hex_digit_display_1 (.value(HEX5));  // open: dp
  Hex_Digit_Display hex_digit_display_2 (.value(HEX4));  // open: dp
  LED L9 (.in(S9));
  LED L8 (.in(S8));
  LED L7 (.in(S7));
  Hex_Digit_Display hex_digit_display_3 (.value(HEX3));  // open: dp
  LED L6 (.in(S6));
  LED L4 (.in(S4));
  LED L5 (.in(S5));
  Hex_Digit_Display hex_digit_display_4 (.value(HEX2));  // open: dp
  Hex_Digit_Display hex_digit_display_5 (.value(HEX1));  // open: dp
  LED L2 (.in(S2));
  LED L3 (.in(S3));
  Hex_Digit_Display hex_digit_display_6 (.value(HEX0));  // open: dp
  LED L1 (.in(S1));
  LED L0 (.in(S0));
  Button u_K3 (.out(K3));
  Button u_K2 (.out(K2));
  Button u_K1 (.out(K1));
  Button u_K0 (.out(K0));
endmodule
