// Logisim project TESTEs.circ as structural Verilog: 1 circuit, main circuit main
module main (
  input  [2:0] in_1,
  input  in_2,
  input  in_3,
  input  in_4,
  input  [3:0] in_5,
  input  in_6,
  input  in_7,
  input  in_8,
  output out_9,
  output out_10,
  output [3:0] out_11,
  output out_12,
  output out_13
);

  // VHDL_Entity #(.content("library ieee;\nuse ieee.std_logic_1164.all;\nuse ieee.numeric_std.all;\n\nentity maq_refri is\n    -- entrada: 0: nada, 2: 10 cent, 3: 25 cent, 4 : 50 cent, 5: 1 real\n    port (\n        entrada : in std_logic_vector(2 downto 0) := \"000\";\n        botao, rst, clk : in std_logic;\n        refri : out std_logic := '0';\n        devolve : out std_logic := '0'\n    );\n\nend maq_refri;\n\narchitecture arch_refri of maq_refri is\n\n    type state_t is (refri_idle, refri_give, refri_reset);\n\n    signal current_state : state_t := refri_idle;\n    signal next_state : state_t := refri_idle;\n    signal grana_total : integer range 0 to 63 := 0;\n\nbegin\n\n    impr:process(current_state, next_state, grana_total, botao) is\n	begin\n		if (current_state'EVENT) then\n	    		report \"----------> CHANGE IN current_state: \" & state_t'image(current_state);\n	  	elsif (next_state'EVENT) then\n	  		report \"----------> CHANGE IN next_state: \" & state_t'image(next_state);\n	  	elsif (grana_total'EVENT) then\n	  		report \"----------> CHANGE IN GRANA: \" & integer'image(grana_total);\n	  	elsif (botao'EVENT) then\n	  		report \"----------> CHANGE IN BOTAO: \" & std_logic'image(botao);\n	  	end if;\n	end process;\n\n    comb:process(clk) is\n    begin\n        if falling_edge(clk) then\n            next_state <= current_state;\n            \n            case current_state is\n                when refri_idle =>\n\n                    devolve <= '0';\n                    refri <= '0';\n\n                    if botao = '1' then\n\n                        if grana_total = 20 then\n                            next_state <= refri_give;\n                        else\n                            next_state <= refri_reset;\n                        end if;\n\n                    else \n                        if grana_total > 20 then\n                            next_state <= refri_reset;\n                        else \n                            next_state <= refri_idle;\n                        end if;\n\n                    end if;\n\n                    \n                when refri_give =>\n\n                    devolve <= '0';\n                    refri <= '1';\n\n                    next_state <= refri_idle;\n                    \n                when refri_reset =>\n                    devolve <= '1';\n                    next_state <= refri_idle;\n            end case;\n\n            -- report \"grana total clock comb: \" & integer'image(grana_total);\n            -- report \"current_state \" & state_t'image(current_state);\n            -- report \"next_state \" & state_t'image(next_state);\n\n        end if;\n    end process comb;\n\n    mem:process(rst, clk) is\n    begin\n        if rising_edge(clk) then\n\n            if rst = '1' then\n                current_state <= refri_idle;\n            else\n                current_state <= next_state;\n\n            end if;\n\n            if next_state = refri_reset or next_state = refri_give or rst = '1' then\n                grana_total <= 0;\n            else \n                case entrada is\n\n                    when \"010\" =>\n                        grana_total <= grana_total + 2;\n                    when \"011\" =>\n                        grana_total <= grana_total + 5;\n                    when \"100\" => \n                        grana_total <= grana_total + 10;\n                    when \"101\" => \n                        grana_total <= grana_total + 20;\n                    when others =>\n                        null;\n                end case;\n\n            end if;\n        end if;\n        -- report \"grana total clock mem: \" & integer'image(grana_total);\n        -- report \"current_state \" & state_t'image(current_state);\n        -- report \"next_state \" & state_t'image(next_state);\n    end process mem;\nend arch_refri;")) vhdl_entity_1: pin names not known; wires that end beside it: in_1, in_2, in_3, in_4, out_9, out_10
  // VHDL_Entity #(.content("library ieee;\nuse ieee.std_logic_1164.all;\nuse ieee.numeric_std.all;\n\nentity elevador is\n    port (\n        andar_requisitado: in std_logic_vector(3 downto 0);\n        --requisitado indica se tem alguem chamando o elevador\n        clk, requisitado, rst: in std_logic;\n        --posicao atual do elevador\n        posicao_output: out std_logic_vector(3 downto 0) := \"0000\";\n        --direcao: '0' indica descendo, '1' indica subindo\n        direcao: out std_logic := '0';\n        --andando: '0' indica parado, '1' indica que esta andando\n        andando: out std_logic := '0'\n    );\n\nend elevador;\n\narchitecture arch_elevador of elevador is\n\n    type state_t is (up, down, stop);\n\n    --signal andar : integer range 0 to 15 := 0;\n    signal current_state : state_t := stop;\n    signal next_state : state_t;\n    signal destino : std_logic_vector(3 downto 0) := \"0000\";\n\n    signal posicao : std_logic_vector(3 downto 0) := \"0000\";\n\n    constant subindo : std_logic := '1';\n    constant descendo : std_logic := '0';\n\nbegin\n\n    impr:process(current_state, next_state, destino, posicao) is\n    begin\n		if (current_state'EVENT) then\n	    	report \"----------> CHANGE IN current_state: \" & state_t'image(current_state);\n		elsif (next_state'EVENT) then\n			report \"----------> CHANGE IN next_state: \" & state_t'image(next_state);\n	  	--elsif (destino'EVENT) then\n			--report \"----------> CHANGE IN DESTINO: \" & unsigned'image(unsigned(destino));\n		--elsif (posicao'EVENT) then\n			--report \"----------> CHANGE IN POSICAO: \" & unsigned'image(unsigned(posicao));\n		end if;\n    end process impr;\n\n    comb:process(clk) is \n    begin\n        if rising_edge(clk) then\n\n            next_state <= current_state;\n            posicao_output <= posicao;\n\n            case current_state is \n                when stop =>\n\n                    andando <= '0';\n\n                    if requisitado = '1' and posicao /= destino then\n\n                        if posicao < destino then\n                            next_state <= up;\n                        else \n                            next_state <= down;\n                        end if;\n\n                    end if;\n\n                when up =>\n\n                    if posicao = andar_requisitado then\n                        next_state <= stop;\n                    end if;\n\n                    andando <= '1';\n                    direcao <= subindo;\n\n                when down =>\n\n                    if posicao = andar_requisitado then \n                        next_state <= stop;\n                    end if;\n\n                    andando <= '1';\n                    direcao <= descendo;\n\n            end case;\n        end if;\n\n    end process comb;\n\n    mem:process(clk) is \n    begin\n        if rst = '1' then\n\n            current_state <= stop;\n            -- andando <= '0';\n            posicao <= \"0000\";\n\n        elsif falling_edge(clk) then\n\n            destino <= andar_requisitado;\n            current_state <= next_state;\n\n            if next_state = up then\n                posicao <= std_logic_vector(unsigned(posicao) + 1);\n            elsif next_state = down then\n                posicao <= std_logic_vector(unsigned(posicao) - 1);\n            end if;\n\n        end if;\n\n    end process mem;\n\n    \n\nend arch_elevador;")) vhdl_entity_2: pin names not known; wires that end beside it: in_5, in_6, in_7, in_8, out_11, out_12, out_13
endmodule
