// Logisim project Inversores.circ as structural Verilog: 2 circuits, main circuit MAIN_Inversores
module MAIN_Inversores (
);

  IntCondInv16 intcondinv16_1 ();  // open: A, Conditinal, S
endmodule

module IntCondInv16 (
  input  [15:0] A,
  input  Conditinal,
  output [15:0] S
);

  wire [15:0] not_1_out;

  assign not_1_out = ~A;  // NOT_Gate not_1, 16 bits wide
  Multiplexer #(.width(16)) multiplexer_1 (.in0(not_1_out), .in1(A), .out(S), .sel(Conditinal));
endmodule
