// Logisim project Somadores.circ as structural Verilog: 3 circuits, main circuit MyAdder
module MAIN_Somadores (
);

  MyAdder myadder_1 ();  // open: A, B, S, Cout
  MyFullAdder myfulladder_1 ();  // open: A, B, Cin, S, Cout
endmodule

module MyAdder (
  input  A,
  input  B,
  output S,
  output Cout
);

  xor xor_1 (S, B, A);
  and and_1 (Cout, B, A);
endmodule

module MyFullAdder (
  input  A,
  input  B,
  input  Cin,
  output S,
  output Cout
);

  wire and_1_out, and_2_out, and_3_out, xor_1_out;

  xor xor_1 (xor_1_out, B, A);
  and and_1 (and_1_out, Cin, B);
  and and_2 (and_2_out, Cin, A);
  and and_3 (and_3_out, B, A);
  xor xor_2 (S, Cin, xor_1_out);
  or or_1 (Cout, and_1_out, and_2_out, and_3_out);
endmodule
