// Logisim project Aritmetica.circ as structural Verilog
module IntAdder16 (
  input  [15:0] A,
  input  [15:0] B,
  input  AddOrSub,
  output [15:0] S
);

  wire myfulladder_1_cout, myfulladder_2_cout, myfulladder_3_cout, myfulladder_4_cout, myfulladder_5_cout,
       myfulladder_6_cout, myfulladder_7_cout, myfulladder_8_cout, myfulladder_9_cout, myfulladder_10_cout,
       myfulladder_11_cout, myfulladder_12_cout, myfulladder_13_cout, myfulladder_14_cout,
       myfulladder_15_cout, not_1_out;
  wire [15:0] intcondinv16_1_s;

  IntCondInv16 intcondinv16_1 (.A(B), .Conditinal(AddOrSub), .S(intcondinv16_1_s));
  not not_1 (not_1_out, AddOrSub);
  MyFullAdder myfulladder_1 (.A(intcondinv16_1_s[0]), .B(A[0]), .Cin(not_1_out), .S(S[0]), .Cout(myfulladder_1_cout));
  MyFullAdder myfulladder_2 (
    .A(intcondinv16_1_s[1]), .B(A[1]), .Cin(myfulladder_1_cout), .S(S[1]), .Cout(myfulladder_2_cout));
  MyFullAdder myfulladder_3 (
    .A(intcondinv16_1_s[2]), .B(A[2]), .Cin(myfulladder_2_cout), .S(S[2]), .Cout(myfulladder_3_cout));
  MyFullAdder myfulladder_4 (
    .A(intcondinv16_1_s[3]), .B(A[3]), .Cin(myfulladder_3_cout), .S(S[3]), .Cout(myfulladder_4_cout));
  MyFullAdder myfulladder_5 (
    .A(intcondinv16_1_s[4]), .B(A[4]), .Cin(myfulladder_4_cout), .S(S[4]), .Cout(myfulladder_5_cout));
  MyFullAdder myfulladder_6 (
    .A(intcondinv16_1_s[5]), .B(A[5]), .Cin(myfulladder_5_cout), .S(S[5]), .Cout(myfulladder_6_cout));
  MyFullAdder myfulladder_7 (
    .A(intcondinv16_1_s[6]), .B(A[6]), .Cin(myfulladder_6_cout), .S(S[6]), .Cout(myfulladder_7_cout));
  MyFullAdder myfulladder_8 (
    .A(intcondinv16_1_s[7]), .B(A[7]), .Cin(myfulladder_7_cout), .S(S[7]), .Cout(myfulladder_8_cout));
  MyFullAdder myfulladder_9 (
    .A(intcondinv16_1_s[8]), .B(A[8]), .Cin(myfulladder_8_cout), .S(S[8]), .Cout(myfulladder_9_cout));
  MyFullAdder myfulladder_10 (
    .A(intcondinv16_1_s[9]), .B(A[9]), .Cin(myfulladder_9_cout), .S(S[9]), .Cout(myfulladder_10_cout));
  MyFullAdder myfulladder_11 (
    .A(intcondinv16_1_s[10]), .B(A[10]), .Cin(myfulladder_10_cout), .S(S[10]), .Cout(myfulladder_11_cout));
  MyFullAdder myfulladder_12 (
    .A(intcondinv16_1_s[11]), .B(A[11]), .Cin(myfulladder_11_cout), .S(S[11]), .Cout(myfulladder_12_cout));
  MyFullAdder myfulladder_13 (
    .A(intcondinv16_1_s[12]), .B(A[12]), .Cin(myfulladder_12_cout), .S(S[12]), .Cout(myfulladder_13_cout));
  MyFullAdder myfulladder_14 (
    .A(intcondinv16_1_s[13]), .B(A[13]), .Cin(myfulladder_13_cout), .S(S[13]), .Cout(myfulladder_14_cout));
  MyFullAdder myfulladder_15 (
    .A(intcondinv16_1_s[14]), .B(A[14]), .Cin(myfulladder_14_cout), .S(S[14]), .Cout(myfulladder_15_cout));
  MyFullAdder myfulladder_16 (.A(intcondinv16_1_s[15]), .B(A[15]), .Cin(myfulladder_15_cout), .S(S[15]));  // open: Cout
endmodule
