// Logisim project UnidadesAritmeticas.circ as structural Verilog
module Arith16_ICMC (
  input  [2:0] OP,
  input  isC,
  input  [15:0] RY,
  input  [15:0] RZ,
  output [15:0] RX
);
endmodule
